# Fritzing sketch hw (saved by Fritzing 0.9.1b)
breadboards: 1

parts:
  IR1 = TSOP312.., 314.. [package=THT]
  元件1 = Arduino Uno (Rev3)
  LED1 = smd LED [color="Red (633nm)" package="0805 [SMD]"]
  S1 = Pushbutton [package="[THT]"]
  LED2 = LED - 5mm [color="Red (633nm)" package="5 mm [THT]"]
  R1 = Resistor [tolerance=±5% resistance=220 package=THT]
  R2 = Resistor [tolerance=±5% resistance=220 package=THT]

nets:
  GND: IR1.GND, 元件1.GND, R1.Pin_1, R2.Pin_1
  N1: IR1.Vs, 元件1.5V
  N2: IR1.Data, 元件1.D11_PWM/MOSI
  N3: 元件1.D13/SCK, LED2.anode
  N4: 元件1.D3_PWM, LED1.anode
  N5: LED1.cathode, R2.Pin_0
  N6: S1.Pin_1, S1.Pin_2
  N7: S1.Pin_3, S1.Pin_4
  N8: LED2.cathode, R1.Pin_0
